// Logisim project snake.circ as structural Verilog: 8 circuits, main circuit main
module main (
  output [1:0] out_1,
  output [2:0] out_2,
  output [6:0] out_3
);

  wire clock_1_out, clock_2_out, clock_3_out, clock_4_out, clock_5_out, comparator_2_eq, comparator_3_eq,
       comparator_4_eq, comparator_5_eq, controlled_buffer_1_out, controlled_buffer_2_out, down, Err,
       keyboard_1_avail, keyboard_2_avail, L, movement_1_stop, movement_1_value, or_2_out, or_4_out, R, up;
  wire [3:0] adder_1_out, adder_2_out, multiplexer_1_out, multiplexer_2_out, multiplexer_3_out,
       multiplexer_4_out, multiplexer_5_out, multiplexer_6_out, or_1_out, or_3_out, register_1_q,
       register_2_q, X, x_food, X_head, X_tail, Y, y_food, Y_head, Y_tail;
  wire [6:0] keyboard_1_data;
  wire [15:0] data_to_screen_1_out_9, data_to_screen_1_out_10, data_to_screen_1_out_11,
       data_to_screen_1_out_12, data_to_screen_1_out_13, data_to_screen_1_out_14, data_to_screen_1_out_15,
       data_to_screen_1_out_16, data_to_screen_1_out_17, data_to_screen_1_out_18, data_to_screen_1_out_19,
       data_to_screen_1_out_20, data_to_screen_1_out_21, data_to_screen_1_out_22, data_to_screen_1_out_23,
       data_to_screen_1_out_24, update_to_screen_1_out_18, update_to_screen_1_out_19,
       update_to_screen_1_out_20, update_to_screen_1_out_21, update_to_screen_1_out_22,
       update_to_screen_1_out_23, update_to_screen_1_out_24, update_to_screen_1_out_25,
       update_to_screen_1_out_26, update_to_screen_1_out_27, update_to_screen_1_out_28,
       update_to_screen_1_out_29, update_to_screen_1_out_30, update_to_screen_1_out_31,
       update_to_screen_1_out_32, update_to_screen_1_out_33;

  Clock clock_1 (.out(clock_1_out));
  food_generation food_generation_1 (
    .Count(out_2), .head_x(X_head), .head_y(Y_head), .Error(Err), .food_x(x_food), .food_y(y_food));
  Multiplexer #(.width(4)) multiplexer_1 (.in0(4'b0000), .in1(4'b0001), .out(multiplexer_1_out), .sel(R));  // open: en
  Multiplexer #(.width(4)) multiplexer_2 (
    .in0(4'b0000), .in1(4'b0001), .out(multiplexer_2_out), .sel(down));  // open: en
  direction direction_1 (.UP(up), .DOWN(down), .Clock(clock_1_out), .LEFT(L), .RIGHT(R), .State(out_1));
  assign or_1_out = multiplexer_1_out | multiplexer_3_out;  // OR_Gate or_1, 4 bits wide
  or or_2 (or_2_out, L, R);
  Multiplexer #(.width(4)) multiplexer_3 (.in0(4'b0000), .in1(4'b1111), .out(multiplexer_3_out), .sel(L));  // open: en
  assign or_3_out = multiplexer_2_out | multiplexer_4_out;  // OR_Gate or_3, 4 bits wide
  or or_4 (or_4_out, up, down);
  Multiplexer #(.width(4)) multiplexer_4 (.in0(4'b0000), .in1(4'b1111), .out(multiplexer_4_out), .sel(up));  // open: en
  Multiplexer #(.width(4)) multiplexer_5 (
    .in0(4'b0000), .in1(or_1_out), .out(multiplexer_5_out), .sel(or_2_out));  // open: en
  Clock clock_2 (.out(clock_2_out));
  Multiplexer #(.width(4)) multiplexer_6 (
    .in0(4'b0000), .in1(or_3_out), .out(multiplexer_6_out), .sel(or_4_out));  // open: en
  Adder #(.width(4)) adder_1 (.a(register_1_q), .b(multiplexer_5_out), .out(adder_1_out));  // open: cin, cout
  Register #(.width(4)) register_1 (.D(adder_1_out), .Q(register_1_q), .clk(clock_2_out));  // open: en, clr
  Register #(.width(4)) register_2 (.D(adder_2_out), .Q(register_2_q), .clk(clock_2_out));  // open: en, clr
  Adder #(.width(4)) adder_2 (.a(register_2_q), .b(multiplexer_6_out), .out(adder_2_out));  // open: cin, cout
  Comparator #(.width(3)) comparator_1 (.a(out_2), .b(3'b010));  // open: gt, eq, lt
  Comparator #(.width(3)) comparator_2 (.a(out_2), .b(3'b001), .eq(comparator_2_eq));  // open: gt, lt
  Clock clock_3 (.out(clock_3_out));
  movement movement_1 (
    .Direction(out_1), .X_head(X_head), .Y_head(Y_head), .X_tail(X_tail), .Y_tail(Y_tail),
    .Value(movement_1_value), .Stop(movement_1_stop), .X(X), .Y(Y), .Clock(clock_3_out), .Counter(out_2));
  Hex_Digit_Display hex_digit_display_1 (.value(register_1_q));  // open: dp
  coords coords_1 (.X(X), .Y(Y), .out_4(X_head), .out_5(Y_head), .Clock(comparator_2_eq));
  Hex_Digit_Display hex_digit_display_2 (.value(register_2_q));  // open: dp
  update_to_screen update_to_screen_1 (
    .update(comparator_3_eq), .in_2(data_to_screen_1_out_9), .in_3(data_to_screen_1_out_10),
    .in_4(data_to_screen_1_out_11), .in_5(data_to_screen_1_out_12), .in_6(data_to_screen_1_out_13),
    .in_7(data_to_screen_1_out_14), .in_8(data_to_screen_1_out_15), .in_9(data_to_screen_1_out_16),
    .in_10(data_to_screen_1_out_17), .in_11(data_to_screen_1_out_18), .in_12(data_to_screen_1_out_19),
    .in_13(data_to_screen_1_out_20), .in_14(data_to_screen_1_out_21), .in_15(data_to_screen_1_out_22),
    .in_16(data_to_screen_1_out_23), .in_17(data_to_screen_1_out_24), .out_18(update_to_screen_1_out_18),
    .out_19(update_to_screen_1_out_19), .out_20(update_to_screen_1_out_20),
    .out_21(update_to_screen_1_out_21), .out_22(update_to_screen_1_out_22),
    .out_23(update_to_screen_1_out_23), .out_24(update_to_screen_1_out_24),
    .out_25(update_to_screen_1_out_25), .out_26(update_to_screen_1_out_26),
    .out_27(update_to_screen_1_out_27), .out_28(update_to_screen_1_out_28),
    .out_29(update_to_screen_1_out_29), .out_30(update_to_screen_1_out_30),
    .out_31(update_to_screen_1_out_31), .out_32(update_to_screen_1_out_32), .out_33(update_to_screen_1_out_33));
  data_to_screen data_to_screen_1 (
    .clock(clock_3_out), .X(X), .Y(Y), .Value(movement_1_value), .Stop(movement_1_stop),
    .out_9(data_to_screen_1_out_9), .out_10(data_to_screen_1_out_10), .out_11(data_to_screen_1_out_11),
    .out_13(data_to_screen_1_out_13), .out_14(data_to_screen_1_out_14), .out_15(data_to_screen_1_out_15),
    .out_16(data_to_screen_1_out_16), .out_17(data_to_screen_1_out_17), .out_18(data_to_screen_1_out_18),
    .out_19(data_to_screen_1_out_19), .out_20(data_to_screen_1_out_20), .out_21(data_to_screen_1_out_21),
    .out_22(data_to_screen_1_out_22), .out_23(data_to_screen_1_out_23), .out_24(data_to_screen_1_out_24),
    .out_12(data_to_screen_1_out_12), .X_FOOD(x_food), .Y_FOOD(y_food), .Error(Err), .counter(out_2));
  Comparator #(.width(3)) comparator_3 (.a(out_2), .b(3'b111), .eq(comparator_3_eq));  // open: gt, lt
  Comparator #(.width(3)) comparator_4 (.a(out_2), .b(3'b101), .eq(comparator_4_eq));  // open: gt, lt
  DotMatrix #(.inputtype("row"), .matrixcols(16), .matrixrows(16)) dotmatrix_1 (
    .row0(update_to_screen_1_out_18), .row1(update_to_screen_1_out_19), .row2(update_to_screen_1_out_20),
    .row3(update_to_screen_1_out_21), .row4(update_to_screen_1_out_22), .row5(update_to_screen_1_out_23),
    .row6(update_to_screen_1_out_24), .row7(update_to_screen_1_out_25), .row8(update_to_screen_1_out_26),
    .row9(update_to_screen_1_out_27), .row10(update_to_screen_1_out_28), .row11(update_to_screen_1_out_29),
    .row12(update_to_screen_1_out_30), .row13(update_to_screen_1_out_31), .row14(update_to_screen_1_out_32),
    .row15(update_to_screen_1_out_33));
  Clock clock_4 (.out(clock_4_out));
  coords coords_2 (.X(X), .Y(Y), .out_4(X_tail), .out_5(Y_tail), .Clock(comparator_4_eq));
  Keyboard keyboard_1 (
    .clk(controlled_buffer_1_out), .avail(keyboard_1_avail), .data(keyboard_1_data));  // open: re, clr
  assign controlled_buffer_1_out = keyboard_1_avail ? clock_4_out : 1'bz;  // Controlled_Buffer controlled_buffer_1
  keyboard_input keyboard_input_1 (.in_1(keyboard_1_data), .left(L), .right(R), .up(up), .down(down));
  Clock clock_5 (.out(clock_5_out));
  assign controlled_buffer_2_out = keyboard_2_avail ? clock_5_out : 1'bz;  // Controlled_Buffer controlled_buffer_2
  Keyboard keyboard_2 (.clk(controlled_buffer_2_out), .avail(keyboard_2_avail), .data(out_3));  // open: re, clr
  Comparator #(.width(7)) comparator_5 (.a(out_3), .b(7'b1100001), .eq(comparator_5_eq));  // open: gt, lt

  // Other names for the same wires on the sheet: counter[2:0] = out_2; direction[1:0] = out_1

  // Notes on the sheet:
  //   Head
  //   Tail
endmodule

module data_to_screen (
  input  [2:0] counter,
  input  clock,
  input  [3:0] X,
  input  [3:0] Y,
  input  Value,
  input  Stop,
  input  [3:0] X_FOOD,
  input  [3:0] Y_FOOD,
  output [15:0] out_9,
  output [15:0] out_10,
  output [15:0] out_11,
  output [15:0] out_12,
  output [15:0] out_13,
  output [15:0] out_14,
  output [15:0] out_15,
  output [15:0] out_16,
  output [15:0] out_17,
  output [15:0] out_18,
  output [15:0] out_19,
  output [15:0] out_20,
  output [15:0] out_21,
  output [15:0] out_22,
  output [15:0] out_23,
  output [15:0] out_24,
  output Error
);

  wire comparator_1_eq, comparator_2_eq, comparator_3_eq, comparator_4_eq, comparator_5_eq, comparator_6_eq,
       comparator_7_eq, comparator_8_eq, comparator_9_eq, comparator_10_eq, comparator_11_eq,
       comparator_12_eq, comparator_13_eq, comparator_14_eq, comparator_15_eq, comparator_16_eq,
       comparator_17_eq, comparator_18_eq, comparator_19_eq, comparator_20_eq, comparator_21_eq,
       multiplexer_2_out, not_1_out, not_2_out, not_3_out, not_5_out, not_6_out, not_7_out, not_8_out,
       not_9_out, not_10_out, not_11_out, not_12_out, not_13_out, not_14_out, not_15_out, not_16_out,
       not_17_out, not_18_out, not_19_out, not_20_out, or_18_out, or_19_out, or_20_out, or_21_out, or_22_out,
       or_23_out, or_24_out, or_25_out, or_26_out, or_27_out, or_28_out, or_29_out, or_30_out, or_31_out,
       or_32_out, or_33_out, Stop_t, Value_t;
  wire [3:0] OLD_X_FOOD, OLD_Y_FOOD, subtractor_1_out, X_t, Y_t;
  wire [15:0] and_2_out, and_3_out, and_4_out, and_5_out, and_6_out, and_7_out, and_8_out, and_9_out,
       and_10_out, and_11_out, and_12_out, and_13_out, and_14_out, and_15_out, and_16_out, and_17_out,
       multiplexer_1_out, multiplexer_3_out, multiplexer_4_out, multiplexer_5_out, multiplexer_6_out,
       multiplexer_7_out, multiplexer_8_out, multiplexer_9_out, multiplexer_10_out, multiplexer_11_out,
       multiplexer_12_out, multiplexer_13_out, multiplexer_14_out, multiplexer_15_out, multiplexer_16_out,
       multiplexer_17_out, multiplexer_18_out, multiplexer_19_out, multiplexer_20_out, multiplexer_21_out,
       multiplexer_22_out, multiplexer_23_out, multiplexer_24_out, multiplexer_25_out, multiplexer_26_out,
       multiplexer_27_out, multiplexer_28_out, multiplexer_29_out, multiplexer_30_out, multiplexer_31_out,
       multiplexer_32_out, multiplexer_33_out, multiplexer_34_out, or_2_out, or_3_out, or_4_out, or_5_out,
       or_6_out, or_7_out, or_8_out, or_9_out, or_10_out, or_11_out, or_12_out, or_13_out, or_14_out,
       or_15_out, or_16_out, or_17_out, shifter_1_out, shifter_2_out, shifter_3_out, shifter_4_out,
       shifter_5_out, shifter_6_out, shifter_7_out, shifter_8_out, shifter_9_out, shifter_10_out,
       shifter_11_out, shifter_12_out, shifter_13_out, shifter_14_out, shifter_15_out, shifter_16_out;

  Comparator #(.width(3)) comparator_1 (.a(counter), .b(3'b110), .eq(comparator_1_eq));  // open: gt, lt
  Comparator #(.width(3)) comparator_2 (.a(counter), .b(3'b110), .eq(comparator_2_eq));  // open: gt, lt
  Transistor #(.\type ("n"), .width(4)) transistor_1 (.in(X_FOOD), .out(X_t), .gate(comparator_1_eq));
  Transistor #(.\type ("n"), .width(4)) transistor_2 (.in(Y_FOOD), .out(Y_t), .gate(comparator_1_eq));
  Transistor #(.\type ("n")) transistor_3 (.in(1'b1), .out(Value_t), .gate(comparator_1_eq));
  Transistor #(.\type ("n")) transistor_4 (.in(1'b0), .out(Stop_t), .gate(comparator_1_eq));
  Transistor #(.\type ("n"), .width(4)) transistor_5 (.in(X_FOOD), .out(OLD_X_FOOD), .gate(comparator_1_eq));
  Transistor #(.\type ("n"), .width(4)) transistor_6 (.in(Y_FOOD), .out(OLD_Y_FOOD), .gate(comparator_1_eq));
  not not_1 (not_1_out, comparator_2_eq);
  Transistor #(.\type ("n"), .width(4)) transistor_7 (.in(X), .out(X_t), .gate(not_1_out));
  Transistor #(.\type ("n"), .width(4)) transistor_8 (.in(Y), .out(Y_t), .gate(not_1_out));
  Transistor #(.\type ("n")) transistor_9 (.in(Value), .out(Value_t), .gate(not_1_out));
  Transistor #(.\type ("n")) transistor_10 (.in(Stop), .out(Stop_t), .gate(not_1_out));
  Multiplexer #(.select(4), .width(16)) multiplexer_1 (
    .in0(out_9), .in1(out_10), .in2(out_11), .in3(out_12), .in4(out_13), .in5(out_14), .in6(out_15),
    .in7(out_16), .in8(out_17), .in9(out_18), .in10(out_19), .in11(out_20), .in12(out_21), .in13(out_22),
    .in14(out_23), .in15(out_24), .out(multiplexer_1_out), .sel(Y_FOOD));  // open: en
  Comparator #(.width(3)) comparator_3 (.a(counter), .b(3'b001), .eq(comparator_3_eq));  // open: gt, lt
  Comparator #(.width(4)) comparator_4 (.a(X_FOOD), .b(OLD_X_FOOD), .eq(comparator_4_eq));  // open: gt, lt
  Comparator #(.width(4)) comparator_5 (.a(Y_FOOD), .b(OLD_Y_FOOD), .eq(comparator_5_eq));  // open: gt, lt
  // AND_Gate and_1 is placed but not wired
  Multiplexer #(.select(4)) multiplexer_2 (
    .in0(multiplexer_1_out[0]), .in1(multiplexer_1_out[1]), .in2(multiplexer_1_out[2]),
    .in3(multiplexer_1_out[3]), .in4(multiplexer_1_out[4]), .in5(multiplexer_1_out[5]),
    .in6(multiplexer_1_out[6]), .in7(multiplexer_1_out[7]), .in8(multiplexer_1_out[8]),
    .in9(multiplexer_1_out[9]), .in10(multiplexer_1_out[10]), .in11(multiplexer_1_out[11]),
    .in12(multiplexer_1_out[12]), .in13(multiplexer_1_out[13]), .in14(multiplexer_1_out[14]),
    .in15(multiplexer_1_out[15]), .out(multiplexer_2_out), .sel(subtractor_1_out));  // open: en
  not not_2 (not_2_out, comparator_4_eq);
  not not_3 (not_3_out, comparator_5_eq);
  // NOT_Gate not_4 is placed but not wired
  Shifter #(.width(16), .shift("lr")) shifter_1 (.in(16'h8000), .\dist (X_t), .out(shifter_1_out));
  Shifter #(.width(16), .shift("lr")) shifter_2 (.in(16'h8000), .\dist (X_t), .out(shifter_2_out));
  Shifter #(.width(16), .shift("lr")) shifter_3 (.in(16'h8000), .\dist (X_t), .out(shifter_3_out));
  Shifter #(.width(16), .shift("lr")) shifter_4 (.in(16'h8000), .\dist (X_t), .out(shifter_4_out));
  Shifter #(.width(16), .shift("lr")) shifter_5 (.in(16'h8000), .\dist (X_t), .out(shifter_5_out));
  Shifter #(.width(16), .shift("lr")) shifter_6 (.in(16'h8000), .\dist (X_t), .out(shifter_6_out));
  Shifter #(.width(16), .shift("lr")) shifter_7 (.in(16'h8000), .\dist (X_t), .out(shifter_7_out));
  Shifter #(.width(16), .shift("lr")) shifter_8 (.in(16'h8000), .\dist (X_t), .out(shifter_8_out));
  Shifter #(.width(16), .shift("lr")) shifter_9 (.in(16'h8000), .\dist (X_t), .out(shifter_9_out));
  Shifter #(.width(16), .shift("lr")) shifter_10 (.in(16'h8000), .\dist (X_t), .out(shifter_10_out));
  Shifter #(.width(16), .shift("lr")) shifter_11 (.in(16'h8000), .\dist (X_t), .out(shifter_11_out));
  Shifter #(.width(16), .shift("lr")) shifter_12 (.in(16'h8000), .\dist (X_t), .out(shifter_12_out));
  Shifter #(.width(16), .shift("lr")) shifter_13 (.in(16'h8000), .\dist (X_t), .out(shifter_13_out));
  Shifter #(.width(16), .shift("lr")) shifter_14 (.in(16'h8000), .\dist (X_t), .out(shifter_14_out));
  Shifter #(.width(16), .shift("lr")) shifter_15 (.in(16'h8000), .\dist (X_t), .out(shifter_15_out));
  Shifter #(.width(16), .shift("lr")) shifter_16 (.in(16'h8000), .\dist (X_t), .out(shifter_16_out));
  // Probe on subtractor_1_out
  Subtractor #(.width(4)) subtractor_1 (.a(4'b1111), .b(X_FOOD), .out(subtractor_1_out));  // open: bin, bout
  // OR_Gate or_1 is placed but not wired
  assign and_2_out = ~shifter_1_out & out_9;  // AND_Gate and_2, 16 bits wide
  Multiplexer #(.width(16)) multiplexer_3 (
    .in0(and_2_out), .in1(or_2_out), .out(multiplexer_3_out), .sel(Value_t));  // open: en
  assign or_2_out = out_9 | shifter_1_out;  // OR_Gate or_2, 16 bits wide
  not not_5 (not_5_out, comparator_6_eq);
  Comparator #(.width(4), .mode("unsigned")) comparator_6 (.a(Y_t), .b(4'b0000), .eq(comparator_6_eq));  // open: gt, lt
  assign and_3_out = ~shifter_2_out & out_10;  // AND_Gate and_3, 16 bits wide
  Multiplexer #(.width(16)) multiplexer_4 (
    .in0(and_3_out), .in1(or_3_out), .out(multiplexer_4_out), .sel(Value_t));  // open: en
  assign or_3_out = out_10 | shifter_2_out;  // OR_Gate or_3, 16 bits wide
  not not_6 (not_6_out, comparator_7_eq);
  Comparator #(.width(4), .mode("unsigned")) comparator_7 (.a(Y_t), .b(4'b0001), .eq(comparator_7_eq));  // open: gt, lt
  assign and_4_out = ~shifter_3_out & out_11;  // AND_Gate and_4, 16 bits wide
  Multiplexer #(.width(16)) multiplexer_5 (
    .in0(and_4_out), .in1(or_4_out), .out(multiplexer_5_out), .sel(Value_t));  // open: en
  assign or_4_out = out_11 | shifter_3_out;  // OR_Gate or_4, 16 bits wide
  not not_7 (not_7_out, comparator_8_eq);
  Comparator #(.width(4), .mode("unsigned")) comparator_8 (.a(Y_t), .b(4'b0010), .eq(comparator_8_eq));  // open: gt, lt
  assign and_5_out = ~shifter_4_out & out_12;  // AND_Gate and_5, 16 bits wide
  Multiplexer #(.width(16)) multiplexer_6 (
    .in0(and_5_out), .in1(or_5_out), .out(multiplexer_6_out), .sel(Value_t));  // open: en
  assign or_5_out = out_12 | shifter_4_out;  // OR_Gate or_5, 16 bits wide
  not not_8 (not_8_out, comparator_9_eq);
  Comparator #(.width(4), .mode("unsigned")) comparator_9 (.a(Y_t), .b(4'b0011), .eq(comparator_9_eq));  // open: gt, lt
  assign and_6_out = ~shifter_5_out & out_13;  // AND_Gate and_6, 16 bits wide
  Multiplexer #(.width(16)) multiplexer_7 (
    .in0(and_6_out), .in1(or_6_out), .out(multiplexer_7_out), .sel(Value_t));  // open: en
  assign or_6_out = out_13 | shifter_5_out;  // OR_Gate or_6, 16 bits wide
  Comparator #(.width(4), .mode("unsigned")) comparator_10 (
    .a(Y_t), .b(4'b0100), .eq(comparator_10_eq));  // open: gt, lt
  not not_9 (not_9_out, comparator_10_eq);
  assign and_7_out = ~shifter_6_out & out_14;  // AND_Gate and_7, 16 bits wide
  Multiplexer #(.width(16)) multiplexer_8 (
    .in0(and_7_out), .in1(or_7_out), .out(multiplexer_8_out), .sel(Value_t));  // open: en
  assign or_7_out = out_14 | shifter_6_out;  // OR_Gate or_7, 16 bits wide
  Comparator #(.width(4), .mode("unsigned")) comparator_11 (
    .a(Y_t), .b(4'b0101), .eq(comparator_11_eq));  // open: gt, lt
  not not_10 (not_10_out, comparator_11_eq);
  assign and_8_out = ~shifter_7_out & out_15;  // AND_Gate and_8, 16 bits wide
  Multiplexer #(.width(16)) multiplexer_9 (
    .in0(and_8_out), .in1(or_8_out), .out(multiplexer_9_out), .sel(Value_t));  // open: en
  assign or_8_out = out_15 | shifter_7_out;  // OR_Gate or_8, 16 bits wide
  not not_11 (not_11_out, comparator_12_eq);
  Comparator #(.width(4), .mode("unsigned")) comparator_12 (
    .a(Y_t), .b(4'b0110), .eq(comparator_12_eq));  // open: gt, lt
  assign and_9_out = ~shifter_8_out & out_16;  // AND_Gate and_9, 16 bits wide
  Multiplexer #(.width(16)) multiplexer_10 (
    .in0(and_9_out), .in1(or_9_out), .out(multiplexer_10_out), .sel(Value_t));  // open: en
  assign or_9_out = out_16 | shifter_8_out;  // OR_Gate or_9, 16 bits wide
  Comparator #(.width(4), .mode("unsigned")) comparator_13 (
    .a(Y_t), .b(4'b0111), .eq(comparator_13_eq));  // open: gt, lt
  not not_12 (not_12_out, comparator_13_eq);
  assign and_10_out = ~shifter_9_out & out_17;  // AND_Gate and_10, 16 bits wide
  Multiplexer #(.width(16)) multiplexer_11 (
    .in0(and_10_out), .in1(or_10_out), .out(multiplexer_11_out), .sel(Value_t));  // open: en
  assign or_10_out = out_17 | shifter_9_out;  // OR_Gate or_10, 16 bits wide
  Comparator #(.width(4), .mode("unsigned")) comparator_14 (
    .a(Y_t), .b(4'b1000), .eq(comparator_14_eq));  // open: gt, lt
  not not_13 (not_13_out, comparator_14_eq);
  assign and_11_out = ~shifter_10_out & out_18;  // AND_Gate and_11, 16 bits wide
  Multiplexer #(.width(16)) multiplexer_12 (
    .in0(and_11_out), .in1(or_11_out), .out(multiplexer_12_out), .sel(Value_t));  // open: en
  assign or_11_out = out_18 | shifter_10_out;  // OR_Gate or_11, 16 bits wide
  not not_14 (not_14_out, comparator_15_eq);
  Comparator #(.width(4), .mode("unsigned")) comparator_15 (
    .a(Y_t), .b(4'b1001), .eq(comparator_15_eq));  // open: gt, lt
  assign and_12_out = ~shifter_11_out & out_19;  // AND_Gate and_12, 16 bits wide
  Multiplexer #(.width(16)) multiplexer_13 (
    .in0(and_12_out), .in1(or_12_out), .out(multiplexer_13_out), .sel(Value_t));  // open: en
  assign or_12_out = out_19 | shifter_11_out;  // OR_Gate or_12, 16 bits wide
  Comparator #(.width(4), .mode("unsigned")) comparator_16 (
    .a(Y_t), .b(4'b1010), .eq(comparator_16_eq));  // open: gt, lt
  not not_15 (not_15_out, comparator_16_eq);
  assign and_13_out = ~shifter_12_out & out_20;  // AND_Gate and_13, 16 bits wide
  Multiplexer #(.width(16)) multiplexer_14 (
    .in0(and_13_out), .in1(or_13_out), .out(multiplexer_14_out), .sel(Value_t));  // open: en
  assign or_13_out = out_20 | shifter_12_out;  // OR_Gate or_13, 16 bits wide
  Comparator #(.width(4), .mode("unsigned")) comparator_17 (
    .a(Y_t), .b(4'b1011), .eq(comparator_17_eq));  // open: gt, lt
  not not_16 (not_16_out, comparator_17_eq);
  assign and_14_out = ~shifter_13_out & out_21;  // AND_Gate and_14, 16 bits wide
  Multiplexer #(.width(16)) multiplexer_15 (
    .in0(and_14_out), .in1(or_14_out), .out(multiplexer_15_out), .sel(Value_t));  // open: en
  assign or_14_out = out_21 | shifter_13_out;  // OR_Gate or_14, 16 bits wide
  not not_17 (not_17_out, comparator_18_eq);
  Comparator #(.width(4), .mode("unsigned")) comparator_18 (
    .a(Y_t), .b(4'b1100), .eq(comparator_18_eq));  // open: gt, lt
  assign and_15_out = ~shifter_14_out & out_22;  // AND_Gate and_15, 16 bits wide
  Multiplexer #(.width(16)) multiplexer_16 (
    .in0(and_15_out), .in1(or_15_out), .out(multiplexer_16_out), .sel(Value_t));  // open: en
  assign or_15_out = out_22 | shifter_14_out;  // OR_Gate or_15, 16 bits wide
  Comparator #(.width(4), .mode("unsigned")) comparator_19 (
    .a(Y_t), .b(4'b1101), .eq(comparator_19_eq));  // open: gt, lt
  not not_18 (not_18_out, comparator_19_eq);
  assign and_16_out = ~shifter_15_out & out_23;  // AND_Gate and_16, 16 bits wide
  Multiplexer #(.width(16)) multiplexer_17 (
    .in0(and_16_out), .in1(or_16_out), .out(multiplexer_17_out), .sel(Value_t));  // open: en
  assign or_16_out = out_23 | shifter_15_out;  // OR_Gate or_16, 16 bits wide
  not not_19 (not_19_out, comparator_20_eq);
  Comparator #(.width(4), .mode("unsigned")) comparator_20 (
    .a(Y_t), .b(4'b1110), .eq(comparator_20_eq));  // open: gt, lt
  assign and_17_out = ~shifter_16_out & out_24;  // AND_Gate and_17, 16 bits wide
  Multiplexer #(.width(16)) multiplexer_18 (
    .in0(and_17_out), .in1(or_17_out), .out(multiplexer_18_out), .sel(Value_t));  // open: en
  assign or_17_out = out_24 | shifter_16_out;  // OR_Gate or_17, 16 bits wide
  Comparator #(.width(4), .mode("unsigned")) comparator_21 (
    .a(Y_t), .b(4'b1111), .eq(comparator_21_eq));  // open: gt, lt
  not not_20 (not_20_out, comparator_21_eq);
  or or_18 (or_18_out, Stop_t, not_5_out);
  or or_19 (or_19_out, Stop_t, not_6_out);
  or or_20 (or_20_out, Stop_t, not_7_out);
  Multiplexer #(.width(16)) multiplexer_19 (
    .in0(multiplexer_6_out), .in1(out_12), .out(multiplexer_19_out), .sel(or_21_out));  // open: en
  or or_21 (or_21_out, Stop_t, not_8_out);
  Multiplexer #(.width(16)) multiplexer_20 (
    .in0(multiplexer_7_out), .in1(out_13), .out(multiplexer_20_out), .sel(or_22_out));  // open: en
  or or_22 (or_22_out, Stop_t, not_9_out);
  Multiplexer #(.width(16)) multiplexer_21 (
    .in0(multiplexer_8_out), .in1(out_14), .out(multiplexer_21_out), .sel(or_23_out));  // open: en
  or or_23 (or_23_out, Stop_t, not_10_out);
  Multiplexer #(.width(16)) multiplexer_22 (
    .in0(multiplexer_9_out), .in1(out_15), .out(multiplexer_22_out), .sel(or_24_out));  // open: en
  or or_24 (or_24_out, Stop_t, not_11_out);
  Multiplexer #(.width(16)) multiplexer_23 (
    .in0(multiplexer_10_out), .in1(out_16), .out(multiplexer_23_out), .sel(or_25_out));  // open: en
  or or_25 (or_25_out, Stop_t, not_12_out);
  Multiplexer #(.width(16)) multiplexer_24 (
    .in0(multiplexer_11_out), .in1(out_17), .out(multiplexer_24_out), .sel(or_26_out));  // open: en
  or or_26 (or_26_out, Stop_t, not_13_out);
  Multiplexer #(.width(16)) multiplexer_25 (
    .in0(multiplexer_12_out), .in1(out_18), .out(multiplexer_25_out), .sel(or_27_out));  // open: en
  or or_27 (or_27_out, Stop_t, not_14_out);
  Multiplexer #(.width(16)) multiplexer_26 (
    .in0(multiplexer_13_out), .in1(out_19), .out(multiplexer_26_out), .sel(or_28_out));  // open: en
  or or_28 (or_28_out, Stop_t, not_15_out);
  Multiplexer #(.width(16)) multiplexer_27 (
    .in0(multiplexer_14_out), .in1(out_20), .out(multiplexer_27_out), .sel(or_29_out));  // open: en
  or or_29 (or_29_out, Stop_t, not_16_out);
  Multiplexer #(.width(16)) multiplexer_28 (
    .in0(multiplexer_15_out), .in1(out_21), .out(multiplexer_28_out), .sel(or_30_out));  // open: en
  or or_30 (or_30_out, Stop_t, not_17_out);
  Multiplexer #(.width(16)) multiplexer_29 (
    .in0(multiplexer_16_out), .in1(out_22), .out(multiplexer_29_out), .sel(or_31_out));  // open: en
  or or_31 (or_31_out, Stop_t, not_18_out);
  Multiplexer #(.width(16)) multiplexer_30 (
    .in0(multiplexer_17_out), .in1(out_23), .out(multiplexer_30_out), .sel(or_32_out));  // open: en
  or or_32 (or_32_out, Stop_t, not_19_out);
  Multiplexer #(.width(16)) multiplexer_31 (
    .in0(multiplexer_18_out), .in1(out_24), .out(multiplexer_31_out), .sel(or_33_out));  // open: en
  or or_33 (or_33_out, Stop_t, not_20_out);
  and and_18 (Error, multiplexer_2_out, comparator_3_eq, not_2_out, not_3_out);
  Register #(.width(16)) register_1 (.D(multiplexer_32_out), .Q(out_9), .clk(clock));  // open: en, clr
  Multiplexer #(.width(16)) multiplexer_32 (
    .in0(multiplexer_3_out), .in1(out_9), .out(multiplexer_32_out), .sel(or_18_out));  // open: en
  Register #(.width(16)) register_2 (.D(multiplexer_33_out), .Q(out_10), .clk(clock));  // open: en, clr
  Multiplexer #(.width(16)) multiplexer_33 (
    .in0(multiplexer_4_out), .in1(out_10), .out(multiplexer_33_out), .sel(or_19_out));  // open: en
  Multiplexer #(.width(16)) multiplexer_34 (
    .in0(multiplexer_5_out), .in1(out_11), .out(multiplexer_34_out), .sel(or_20_out));  // open: en
  Register #(.width(16)) register_3 (.D(multiplexer_34_out), .Q(out_11), .clk(clock));  // open: en, clr
  Register #(.width(16)) register_4 (.D(multiplexer_19_out), .Q(out_12), .clk(clock));  // open: en, clr
  Register #(.width(16)) register_5 (.D(multiplexer_20_out), .Q(out_13), .clk(clock));  // open: en, clr
  Register #(.width(16)) register_6 (.D(multiplexer_21_out), .Q(out_14), .clk(clock));  // open: en, clr
  Register #(.width(16)) register_7 (.D(multiplexer_22_out), .Q(out_15), .clk(clock));  // open: en, clr
  Register #(.width(16)) register_8 (.D(multiplexer_23_out), .Q(out_16), .clk(clock));  // open: en, clr
  Register #(.width(16)) register_9 (.D(multiplexer_24_out), .Q(out_17), .clk(clock));  // open: en, clr
  Register #(.width(16)) register_10 (.D(multiplexer_25_out), .Q(out_18), .clk(clock));  // open: en, clr
  Register #(.width(16)) register_11 (.D(multiplexer_26_out), .Q(out_19), .clk(clock));  // open: en, clr
  Register #(.width(16)) register_12 (.D(multiplexer_27_out), .Q(out_20), .clk(clock));  // open: en, clr
  Register #(.width(16)) register_13 (.D(multiplexer_28_out), .Q(out_21), .clk(clock));  // open: en, clr
  Register #(.width(16)) register_14 (.D(multiplexer_29_out), .Q(out_22), .clk(clock));  // open: en, clr
  Register #(.width(16)) register_15 (.D(multiplexer_30_out), .Q(out_23), .clk(clock));  // open: en, clr
  Register #(.width(16)) register_16 (.D(multiplexer_31_out), .Q(out_24), .clk(clock));  // open: en, clr

  // Other names for the same wires on the sheet: _0[15:0] = out_9; _1[15:0] = out_10; _2[15:0] = out_11;
  //   _3[15:0] = out_12; _4[15:0] = out_13; _5[15:0] = out_14; _6[15:0] = out_15; _7[15:0] = out_16;
  //   _8[15:0] = out_17; _9[15:0] = out_18; _10[15:0] = out_19; _11[15:0] = out_20; _12[15:0] = out_21;
  //   _13[15:0] = out_22; _14[15:0] = out_23; _15[15:0] = out_24
endmodule

module direction (
  input  UP,
  input  DOWN,
  input  Clock,
  input  LEFT,
  input  RIGHT,
  output [1:0] State
);

  wire and_2_out, and_3_out, and_4_out, and_5_out, comparator_1_eq, comparator_2_eq, comparator_3_eq,
       comparator_4_eq, or_1_out, or_2_out, or_3_out, or_4_out;
  wire [1:0] transistor_1_out;

  // AND_Gate and_1 is placed but not wired
  Comparator #(.width(2)) comparator_1 (.a(2'b01), .b(State), .eq(comparator_1_eq));  // open: gt, lt
  Comparator #(.width(2)) comparator_2 (.a(2'b00), .b(State), .eq(comparator_2_eq));  // open: gt, lt
  Comparator #(.width(2)) comparator_3 (.a(2'b11), .b(State), .eq(comparator_3_eq));  // open: gt, lt
  Comparator #(.width(2)) comparator_4 (.a(2'b10), .b(State), .eq(comparator_4_eq));  // open: gt, lt
  // NOT_Gate not_1 is placed but not wired
  or or_1 (or_1_out, DOWN, LEFT, RIGHT);
  or or_2 (or_2_out, UP, LEFT, RIGHT);
  or or_3 (or_3_out, UP, DOWN, RIGHT);
  or or_4 (or_4_out, UP, DOWN, LEFT);
  // OR_Gate or_5 is placed but not wired
  and and_2 (and_2_out, ~or_1_out, ~comparator_1_eq, UP);  // AND_Gate
  Transistor #(.\type ("n"), .width(2)) transistor_1 (.in(2'b00), .out(transistor_1_out), .gate(and_2_out));
  and and_3 (and_3_out, ~or_2_out, ~comparator_2_eq, DOWN);  // AND_Gate
  Transistor #(.\type ("n"), .width(2)) transistor_2 (.in(2'b01), .out(transistor_1_out), .gate(and_3_out));
  and and_4 (and_4_out, ~or_3_out, ~comparator_3_eq, LEFT);  // AND_Gate
  Transistor #(.\type ("n"), .width(2)) transistor_3 (.in(2'b10), .out(transistor_1_out), .gate(and_4_out));
  and and_5 (and_5_out, ~or_4_out, ~comparator_4_eq, RIGHT);  // AND_Gate
  Transistor #(.\type ("n"), .width(2)) transistor_4 (.in(2'b11), .out(transistor_1_out), .gate(and_5_out));
  Register #(.width(2)) register_1 (.D(transistor_1_out), .Q(State), .clk(Clock));  // open: en, clr

  // Other names for the same wires on the sheet: D = DOWN; L = LEFT; R = RIGHT; U = UP

  // Notes on the sheet:
  //   State: pull=down
endmodule

module coords (
  input  Clock,
  input  [3:0] X,
  input  [3:0] Y,
  output [3:0] out_4,
  output [3:0] out_5
);

  Register #(.width(4)) register_1 (.D(X), .Q(out_4), .clk(Clock));  // open: en, clr
  Register #(.width(4)) register_2 (.D(Y), .Q(out_5), .clk(Clock));  // open: en, clr
endmodule

module movement (
  input  [1:0] Direction,
  input  Clock,
  input  [3:0] X_head,
  input  [3:0] Y_head,
  input  [3:0] X_tail,
  input  [3:0] Y_tail,
  output [2:0] Counter,
  output Value,
  output Stop,
  output [3:0] X,
  output [3:0] Y
);

  wire and_1_out, and_2_out, comparator_1_eq, comparator_2_eq, comparator_3_eq, comparator_4_lt,
       comparator_5_lt, comparator_6_eq, comparator_7_eq, comparator_8_eq, comparator_9_eq, comparator_11_eq,
       comparator_12_eq, Dir_0, Dir_1, not_1_out, not_2_out, not_3_out, not_4_out, or_1_out, or_2_out,
       or_3_out;
  wire [2:0] adder_1_out;
  wire [3:0] adder_2_out, adder_3_out, adder_4_out, adder_5_out, multiplexer_1_out, multiplexer_2_out,
       multiplexer_3_out, multiplexer_4_out, multiplexer_5_out, multiplexer_6_out, multiplexer_7_out,
       multiplexer_8_out, register_2_q, register_3_q, register_4_q, register_5_q;

  Register #(.width(2)) register_1 (.D(Direction), .Q({Dir_1, Dir_0}), .clk(comparator_1_eq));  // open: en, clr
  Comparator #(.width(3)) comparator_1 (.a(Counter), .b(3'b111), .eq(comparator_1_eq));  // open: gt, lt
  Comparator #(.width(3)) comparator_2 (.a(Counter), .b(3'b000), .eq(comparator_2_eq));  // open: gt, lt
  Comparator #(.width(3)) comparator_3 (.a(Counter), .b(3'b111), .eq(comparator_3_eq));  // open: gt, lt
  Register #(.width(4)) register_2 (.D(X_head), .Q(register_2_q), .clk(comparator_2_eq));  // open: en, clr
  Register #(.width(4)) register_3 (.D(Y_head), .Q(register_3_q), .clk(comparator_2_eq));  // open: en, clr
  Register #(.width(4)) register_4 (.D(X_tail), .Q(register_4_q), .clk(comparator_3_eq));  // open: en, clr
  Register #(.width(4)) register_5 (.D(Y_tail), .Q(register_5_q), .clk(comparator_3_eq));  // open: en, clr
  Multiplexer #(.width(4)) multiplexer_1 (
    .in0(4'b1111), .in1(4'b0001), .out(multiplexer_1_out), .sel(Dir_0));  // open: en
  Multiplexer #(.width(4)) multiplexer_2 (
    .in0(4'b1111), .in1(4'b0001), .out(multiplexer_2_out), .sel(Dir_0));  // open: en
  Multiplexer #(.width(4)) multiplexer_3 (
    .in0(4'b1111), .in1(4'b0001), .out(multiplexer_3_out), .sel(Dir_0));  // open: en
  Multiplexer #(.width(4)) multiplexer_4 (
    .in0(4'b1111), .in1(4'b0001), .out(multiplexer_4_out), .sel(Dir_0));  // open: en
  Adder #(.width(3)) adder_1 (.a(Counter), .b(3'b001), .out(adder_1_out));  // open: cin, cout
  Adder #(.width(4)) adder_2 (.a(multiplexer_1_out), .b(register_2_q), .out(adder_2_out));  // open: cin, cout
  Adder #(.width(4)) adder_3 (.a(multiplexer_2_out), .b(register_3_q), .out(adder_3_out));  // open: cin, cout
  Adder #(.width(4)) adder_4 (.a(multiplexer_3_out), .b(register_4_q), .out(adder_4_out));  // open: cin, cout
  not not_1 (not_1_out, comparator_4_lt);
  Comparator #(.width(3), .mode("unsigned")) comparator_4 (
    .a(Counter), .b(3'b100), .lt(comparator_4_lt));  // open: gt, eq
  Adder #(.width(4)) adder_5 (.a(multiplexer_4_out), .b(register_5_q), .out(adder_5_out));  // open: cin, cout
  Comparator #(.width(3), .mode("unsigned")) comparator_5 (
    .a(Counter), .b(3'b100), .lt(comparator_5_lt));  // open: gt, eq
  not not_2 (not_2_out, comparator_5_lt);
  Register #(.width(3)) register_6 (.D(adder_1_out), .Q(Counter), .clk(Clock));  // open: en, clr
  Multiplexer #(.width(4)) multiplexer_5 (
    .in0(register_2_q), .in1(adder_2_out), .out(multiplexer_5_out), .sel(Dir_1));  // open: en
  Multiplexer #(.width(4)) multiplexer_6 (
    .in0(adder_3_out), .in1(register_3_q), .out(multiplexer_6_out), .sel(Dir_1));  // open: en
  Multiplexer #(.width(4)) multiplexer_7 (
    .in0(register_4_q), .in1(adder_4_out), .out(multiplexer_7_out), .sel(and_1_out));  // open: en
  and and_1 (and_1_out, not_1_out, Dir_1);
  Multiplexer #(.width(4)) multiplexer_8 (
    .in0(adder_5_out), .in1(register_5_q), .out(multiplexer_8_out), .sel(not_3_out));  // open: en
  not not_3 (not_3_out, and_2_out);
  and and_2 (and_2_out, not_2_out, not_4_out);
  not not_4 (not_4_out, Dir_1);
  Multiplexer #(.width(4)) multiplexer_9 (
    .in0(multiplexer_7_out), .in1(multiplexer_5_out), .out(X), .sel(or_1_out));  // open: en
  or or_1 (or_1_out, comparator_6_eq, comparator_7_eq);
  Comparator #(.width(3)) comparator_6 (.a(Counter), .b(3'b000), .eq(comparator_6_eq));  // open: gt, lt
  Comparator #(.width(3)) comparator_7 (.a(Counter), .b(3'b001), .eq(comparator_7_eq));  // open: gt, lt
  Comparator #(.width(3)) comparator_8 (.a(Counter), .b(3'b000), .eq(comparator_8_eq));  // open: gt, lt
  Comparator #(.width(3)) comparator_9 (.a(Counter), .b(3'b001), .eq(comparator_9_eq));  // open: gt, lt
  Comparator #(.width(3)) comparator_10 (.a(Counter), .b(3'b001), .eq(Value));  // open: gt, lt
  Comparator #(.width(3)) comparator_11 (.a(Counter), .b(3'b001), .eq(comparator_11_eq));  // open: gt, lt
  Comparator #(.width(3)) comparator_12 (.a(Counter), .b(3'b011), .eq(comparator_12_eq));  // open: gt, lt
  Multiplexer #(.width(4)) multiplexer_10 (
    .in0(multiplexer_8_out), .in1(multiplexer_6_out), .out(Y), .sel(or_2_out));  // open: en
  or or_2 (or_2_out, comparator_8_eq, comparator_9_eq);
  or or_3 (or_3_out, comparator_11_eq, comparator_12_eq);
  not not_5 (Stop, or_3_out);
  // AND_Gate and_3 is placed but not wired
  // NOT_Gate not_6 is placed but not wired
  // OR_Gate or_4 is placed but not wired
endmodule

module food_generation (
  input  [2:0] Count,
  input  [3:0] head_x,
  input  [3:0] head_y,
  input  Error,
  output [3:0] food_x,
  output [3:0] food_y
);

  wire and_1_out, and_2_out, clock_1_out, comparator_1_eq, comparator_2_eq, comparator_3_eq, or_1_out;

  Comparator #(.width(4)) comparator_1 (.a(food_x), .b(head_x), .eq(comparator_1_eq));  // open: gt, lt
  Comparator #(.width(4)) comparator_2 (.a(food_y), .b(head_y), .eq(comparator_2_eq));  // open: gt, lt
  Comparator #(.width(3)) comparator_3 (.a(Count), .b(3'b101), .eq(comparator_3_eq));  // open: gt, lt
  and and_1 (and_1_out, comparator_1_eq, comparator_2_eq);
  and and_2 (and_2_out, Error, comparator_3_eq);
  or or_1 (or_1_out, and_1_out, and_2_out);
  Clock clock_1 (.out(clock_1_out));
  Random #(.width(4)) random_1 (.clk(clock_1_out), .next(or_1_out), .out(food_x));  // open: clr
  Random #(.width(4)) random_2 (.clk(clock_1_out), .next(or_1_out), .out(food_y));  // open: clr

  // Other names for the same wires on the sheet: Counter[2:0] = Count
endmodule

module update_to_screen (
  input  update,
  input  [15:0] in_2,
  input  [15:0] in_3,
  input  [15:0] in_4,
  input  [15:0] in_5,
  input  [15:0] in_6,
  input  [15:0] in_7,
  input  [15:0] in_8,
  input  [15:0] in_9,
  input  [15:0] in_10,
  input  [15:0] in_11,
  input  [15:0] in_12,
  input  [15:0] in_13,
  input  [15:0] in_14,
  input  [15:0] in_15,
  input  [15:0] in_16,
  input  [15:0] in_17,
  output [15:0] out_18,
  output [15:0] out_19,
  output [15:0] out_20,
  output [15:0] out_21,
  output [15:0] out_22,
  output [15:0] out_23,
  output [15:0] out_24,
  output [15:0] out_25,
  output [15:0] out_26,
  output [15:0] out_27,
  output [15:0] out_28,
  output [15:0] out_29,
  output [15:0] out_30,
  output [15:0] out_31,
  output [15:0] out_32,
  output [15:0] out_33
);

  Register #(.width(16)) register_1 (.D(in_2), .Q(out_18), .clk(update));  // open: en, clr
  Register #(.width(16)) register_2 (.D(in_3), .Q(out_19), .clk(update));  // open: en, clr
  Register #(.width(16)) register_3 (.D(in_4), .Q(out_20), .clk(update));  // open: en, clr
  Register #(.width(16)) register_4 (.D(in_5), .Q(out_21), .clk(update));  // open: en, clr
  Register #(.width(16)) register_5 (.D(in_6), .Q(out_22), .clk(update));  // open: en, clr
  Register #(.width(16)) register_6 (.D(in_7), .Q(out_23), .clk(update));  // open: en, clr
  Register #(.width(16)) register_7 (.D(in_8), .Q(out_24), .clk(update));  // open: en, clr
  Register #(.width(16)) register_8 (.D(in_9), .Q(out_25), .clk(update));  // open: en, clr
  Register #(.width(16)) register_9 (.D(in_10), .Q(out_26), .clk(update));  // open: en, clr
  Register #(.width(16)) register_10 (.D(in_11), .Q(out_27), .clk(update));  // open: en, clr
  Register #(.width(16)) register_11 (.D(in_12), .Q(out_28), .clk(update));  // open: en, clr
  Register #(.width(16)) register_12 (.D(in_13), .Q(out_29), .clk(update));  // open: en, clr
  Register #(.width(16)) register_13 (.D(in_14), .Q(out_30), .clk(update));  // open: en, clr
  Register #(.width(16)) register_14 (.D(in_15), .Q(out_31), .clk(update));  // open: en, clr
  Register #(.width(16)) register_15 (.D(in_16), .Q(out_32), .clk(update));  // open: en, clr
  Register #(.width(16)) register_16 (.D(in_17), .Q(out_33), .clk(update));  // open: en, clr
endmodule

module keyboard_input (
  input  [6:0] in_1,
  output left,
  output right,
  output up,
  output down
);

  Comparator #(.width(7)) comparator_1 (.a(in_1), .b(7'b1100001), .eq(left));  // open: gt, lt
  Comparator #(.width(7)) comparator_2 (.a(in_1), .b(7'b1100100), .eq(right));  // open: gt, lt
  Comparator #(.width(7)) comparator_3 (.a(in_1), .b(7'b1110111), .eq(up));  // open: gt, lt
  Comparator #(.width(7)) comparator_4 (.a(in_1), .b(7'b1110011), .eq(down));  // open: gt, lt

  // Other names for the same wires on the sheet: ascii[6:0] = in_1
endmodule
